// Logisim project Ping-PongHard.circ as structural Verilog: 10 circuits, main circuit main
module videochip (
  input  [4:0] in_1,
  input  [4:0] ballX,
  input  [4:0] ballY,
  input  [4:0] leftbatY,
  input  [4:0] rightbatY,
  output [31:0] out_6,
  output [4:0] out_7,
  output [4:0] leftbatY_2,
  output [4:0] rightbatY_2,
  output [4:0] ballY_2,
  output [4:0] ballX_2
);

  wire comparator_1_eq, comparator_2_eq, comparator_3_eq, or_1_out;
  wire [4:0] multiplexer_1_out;
  wire [31:0] decoder_1_out0;
  wire [31:1] decoder_2_out30;
  wire [31:31] decoder_2_out31;

  Adder #(.width(5)) adder_1 (.a(5'b00001), .b(in_1), .out(out_7));  // open: cin, cout
  Comparator #(.width(5)) comparator_1 (.a(in_1), .b(ballX), .eq(comparator_1_eq));  // open: gt, lt
  Decoder #(.select(5)) decoder_1 (
    .out0(decoder_1_out0[0]), .out1(decoder_1_out0[1]), .out2(decoder_1_out0[2]), .out3(decoder_1_out0[3]),
    .out4(decoder_1_out0[4]), .out5(decoder_1_out0[5]), .out6(decoder_1_out0[6]), .out7(decoder_1_out0[7]),
    .out8(decoder_1_out0[8]), .out9(decoder_1_out0[9]), .out10(decoder_1_out0[10]),
    .out11(decoder_1_out0[11]), .out12(decoder_1_out0[12]), .out13(decoder_1_out0[13]),
    .out14(decoder_1_out0[14]), .out15(decoder_1_out0[15]), .out16(decoder_1_out0[16]),
    .out17(decoder_1_out0[17]), .out18(decoder_1_out0[18]), .out19(decoder_1_out0[19]),
    .out20(decoder_1_out0[20]), .out21(decoder_1_out0[21]), .out22(decoder_1_out0[22]),
    .out23(decoder_1_out0[23]), .out24(decoder_1_out0[24]), .out25(decoder_1_out0[25]),
    .out26(decoder_1_out0[26]), .out27(decoder_1_out0[27]), .out28(decoder_1_out0[28]),
    .out29(decoder_1_out0[29]), .out30(decoder_1_out0[30]), .out31(decoder_1_out0[31]), .sel(ballY),
    .en(comparator_1_eq));
  Comparator #(.width(5)) comparator_2 (.a(in_1), .b(5'b00011), .eq(comparator_2_eq));  // open: gt, lt
  Comparator #(.width(5)) comparator_3 (.a(in_1), .b(5'b11100), .eq(comparator_3_eq));  // open: gt, lt
  or or_1 (or_1_out, comparator_2_eq, comparator_3_eq);
  Multiplexer #(.width(5)) multiplexer_1 (
    .in0(leftbatY), .in1(rightbatY), .out(multiplexer_1_out), .sel(comparator_3_eq), .en(or_1_out));
  Pull_Resistor pull_resistor_1 (.node(decoder_1_out0));
  Decoder #(.select(5)) decoder_2 (
    .out0(decoder_2_out30[1]), .out1(decoder_2_out30[2]), .out2(decoder_2_out30[3]),
    .out3(decoder_2_out30[4]), .out4(decoder_2_out30[5]), .out5(decoder_2_out30[6]),
    .out6(decoder_2_out30[7]), .out7(decoder_2_out30[8]), .out8(decoder_2_out30[9]),
    .out9(decoder_2_out30[10]), .out10(decoder_2_out30[11]), .out11(decoder_2_out30[12]),
    .out12(decoder_2_out30[13]), .out13(decoder_2_out30[14]), .out14(decoder_2_out30[15]),
    .out15(decoder_2_out30[16]), .out16(decoder_2_out30[17]), .out17(decoder_2_out30[18]),
    .out18(decoder_2_out30[19]), .out19(decoder_2_out30[20]), .out20(decoder_2_out30[21]),
    .out21(decoder_2_out30[22]), .out22(decoder_2_out30[23]), .out23(decoder_2_out30[24]),
    .out24(decoder_2_out30[25]), .out25(decoder_2_out30[26]), .out26(decoder_2_out30[27]),
    .out27(decoder_2_out30[28]), .out28(decoder_2_out30[29]), .out29(decoder_2_out30[30]),
    .out30(decoder_2_out30[31]), .out31(decoder_2_out31[31]), .sel(multiplexer_1_out), .en(or_1_out));
  assign out_6 = decoder_1_out0 | {decoder_2_out31[31], decoder_2_out30} | {decoder_2_out30, 1'b0} | {decoder_2_out30[30:1], 2'b00};  // OR_Gate or_2, 32 bits wide
  Pull_Resistor pull_resistor_2 (.node({decoder_2_out31[31], decoder_2_out30}));

  assign ballX_2 = ballX;
  assign ballY_2 = ballY;
  assign leftbatY_2 = leftbatY;
  assign rightbatY_2 = rightbatY;

  // Other names for the same wires on the sheet: BX[4:0] = ballX; BY[4:0] = ballY; CLM[4:0] = out_7;
  //   lftBat[4:0] = leftbatY; rghtBat[4:0] = rightbatY

  // Notes on the sheet:
  //   ColumnID
  //   DiodArray
  //   ColumnID+1
endmodule

module videosegment (
  input  [4:0] in_1,
  input  [4:0] in_2,
  input  [4:0] in_3,
  input  [4:0] in_4,
  input  [4:0] in_5,
  output [31:0] out_6,
  output [31:0] out_7,
  output [31:0] out_8,
  output [31:0] out_9,
  output [31:0] out_10,
  output [31:0] out_11,
  output [31:0] out_12,
  output [31:0] out_13,
  output [4:0] out_14,
  output [4:0] out_15,
  output [4:0] out_16,
  output [4:0] out_17,
  output [4:0] out_18
);

  wire [4:0] videochip_1_ballx_2, videochip_1_bally_2, videochip_1_leftbaty_2, videochip_1_out_7,
       videochip_1_rightbaty_2, videochip_2_ballx_2, videochip_2_bally_2, videochip_2_leftbaty_2,
       videochip_2_out_7, videochip_2_rightbaty_2, videochip_3_ballx_2, videochip_3_bally_2,
       videochip_3_leftbaty_2, videochip_3_out_7, videochip_3_rightbaty_2, videochip_4_ballx_2,
       videochip_4_bally_2, videochip_4_leftbaty_2, videochip_4_out_7, videochip_4_rightbaty_2,
       videochip_5_ballx_2, videochip_5_bally_2, videochip_5_leftbaty_2, videochip_5_out_7,
       videochip_5_rightbaty_2, videochip_6_ballx_2, videochip_6_bally_2, videochip_6_leftbaty_2,
       videochip_6_out_7, videochip_6_rightbaty_2, videochip_7_ballx_2, videochip_7_bally_2,
       videochip_7_leftbaty_2, videochip_7_out_7, videochip_7_rightbaty_2;

  videochip videochip_1 (
    .in_1(in_1), .ballX(in_2), .ballX_2(videochip_1_ballx_2), .ballY(in_3), .ballY_2(videochip_1_bally_2),
    .leftbatY(in_4), .leftbatY_2(videochip_1_leftbaty_2), .rightbatY(in_5),
    .rightbatY_2(videochip_1_rightbaty_2), .out_7(videochip_1_out_7), .out_6(out_6));
  videochip videochip_2 (
    .in_1(videochip_1_out_7), .ballX(videochip_1_ballx_2), .ballX_2(videochip_2_ballx_2),
    .ballY(videochip_1_bally_2), .ballY_2(videochip_2_bally_2), .leftbatY(videochip_1_leftbaty_2),
    .leftbatY_2(videochip_2_leftbaty_2), .rightbatY(videochip_1_rightbaty_2),
    .rightbatY_2(videochip_2_rightbaty_2), .out_7(videochip_2_out_7), .out_6(out_7));
  videochip videochip_3 (
    .in_1(videochip_2_out_7), .ballX(videochip_2_ballx_2), .ballX_2(videochip_3_ballx_2),
    .ballY(videochip_2_bally_2), .ballY_2(videochip_3_bally_2), .leftbatY(videochip_2_leftbaty_2),
    .leftbatY_2(videochip_3_leftbaty_2), .rightbatY(videochip_2_rightbaty_2),
    .rightbatY_2(videochip_3_rightbaty_2), .out_7(videochip_3_out_7), .out_6(out_8));
  videochip videochip_4 (
    .in_1(videochip_3_out_7), .ballX(videochip_3_ballx_2), .ballX_2(videochip_4_ballx_2),
    .ballY(videochip_3_bally_2), .ballY_2(videochip_4_bally_2), .leftbatY(videochip_3_leftbaty_2),
    .leftbatY_2(videochip_4_leftbaty_2), .rightbatY(videochip_3_rightbaty_2),
    .rightbatY_2(videochip_4_rightbaty_2), .out_7(videochip_4_out_7), .out_6(out_9));
  videochip videochip_5 (
    .in_1(videochip_4_out_7), .ballX(videochip_4_ballx_2), .ballX_2(videochip_5_ballx_2),
    .ballY(videochip_4_bally_2), .ballY_2(videochip_5_bally_2), .leftbatY(videochip_4_leftbaty_2),
    .leftbatY_2(videochip_5_leftbaty_2), .rightbatY(videochip_4_rightbaty_2),
    .rightbatY_2(videochip_5_rightbaty_2), .out_7(videochip_5_out_7), .out_6(out_10));
  videochip videochip_6 (
    .in_1(videochip_5_out_7), .ballX(videochip_5_ballx_2), .ballX_2(videochip_6_ballx_2),
    .ballY(videochip_5_bally_2), .ballY_2(videochip_6_bally_2), .leftbatY(videochip_5_leftbaty_2),
    .leftbatY_2(videochip_6_leftbaty_2), .rightbatY(videochip_5_rightbaty_2),
    .rightbatY_2(videochip_6_rightbaty_2), .out_7(videochip_6_out_7), .out_6(out_11));
  videochip videochip_7 (
    .in_1(videochip_6_out_7), .ballX(videochip_6_ballx_2), .ballX_2(videochip_7_ballx_2),
    .ballY(videochip_6_bally_2), .ballY_2(videochip_7_bally_2), .leftbatY(videochip_6_leftbaty_2),
    .leftbatY_2(videochip_7_leftbaty_2), .rightbatY(videochip_6_rightbaty_2),
    .rightbatY_2(videochip_7_rightbaty_2), .out_7(videochip_7_out_7), .out_6(out_12));
  videochip videochip_8 (
    .in_1(videochip_7_out_7), .ballX(videochip_7_ballx_2), .ballX_2(out_15), .ballY(videochip_7_bally_2),
    .ballY_2(out_16), .leftbatY(videochip_7_leftbaty_2), .leftbatY_2(out_17),
    .rightbatY(videochip_7_rightbaty_2), .rightbatY_2(out_18), .out_7(out_14), .out_6(out_13));
endmodule

module main (
);

  wire clock_1_out, R_out;
  wire [4:0] controlchip_1_ballx, controlchip_1_bally, controlchip_1_leftyout, controlchip_1_rightyout,
       controlchip_1_zero, joystick_1_y, not_1_out, videosegment_1_out_14, videosegment_1_out_15,
       videosegment_1_out_16, videosegment_1_out_17, videosegment_1_out_18, videosegment_2_out_14,
       videosegment_2_out_15, videosegment_2_out_16, videosegment_2_out_17, videosegment_2_out_18,
       videosegment_3_out_14, videosegment_3_out_15, videosegment_3_out_16, videosegment_3_out_17,
       videosegment_3_out_18;
  wire [7:0] Ls, Rs;
  wire [31:0] videosegment_1_out_6, videosegment_1_out_7, videosegment_1_out_8, videosegment_1_out_9,
       videosegment_1_out_10, videosegment_1_out_11, videosegment_1_out_12, videosegment_1_out_13,
       videosegment_2_out_6, videosegment_2_out_7, videosegment_2_out_8, videosegment_2_out_9,
       videosegment_2_out_10, videosegment_2_out_11, videosegment_2_out_12, videosegment_2_out_13,
       videosegment_3_out_6, videosegment_3_out_7, videosegment_3_out_8, videosegment_3_out_9,
       videosegment_3_out_10, videosegment_3_out_11, videosegment_3_out_12, videosegment_3_out_13,
       videosegment_4_out_6, videosegment_4_out_7, videosegment_4_out_8, videosegment_4_out_9,
       videosegment_4_out_10, videosegment_4_out_11, videosegment_4_out_12, videosegment_4_out_13;

  Button R (.out(R_out));
  Hex_Digit_Display hex_digit_display_1 (.value(Ls[7:4]));  // open: dp
  Hex_Digit_Display hex_digit_display_2 (.value(Ls[3:0]));  // open: dp
  Joystick #(.bits(5)) joystick_1 (.y(joystick_1_y));  // open: x
  assign not_1_out = ~joystick_1_y;  // NOT_Gate not_1, 5 bits wide
  controlChip controlchip_1 (
    .zero(controlchip_1_zero), .ballX(controlchip_1_ballx), .ballY(controlchip_1_bally),
    .leftYout(controlchip_1_leftyout), .rightYout(controlchip_1_rightyout), .Reset(R_out), .scoreA(Ls),
    .Tacts(clock_1_out), .scoreB(Rs), .leftYin(not_1_out));
  Clock clock_1 (.out(clock_1_out));
  DotMatrix #(.matrixcols(32), .matrixrows(32)) dotmatrix_1 (
    .col0(videosegment_1_out_6), .col1(videosegment_1_out_7), .col2(videosegment_1_out_8),
    .col3(videosegment_1_out_9), .col4(videosegment_1_out_10), .col5(videosegment_1_out_11),
    .col6(videosegment_1_out_12), .col7(videosegment_1_out_13), .col8(videosegment_2_out_6),
    .col9(videosegment_2_out_7), .col10(videosegment_2_out_8), .col11(videosegment_2_out_9),
    .col12(videosegment_2_out_10), .col13(videosegment_2_out_11), .col14(videosegment_2_out_12),
    .col15(videosegment_2_out_13), .col16(videosegment_3_out_6), .col17(videosegment_3_out_7),
    .col18(videosegment_3_out_8), .col19(videosegment_3_out_9), .col20(videosegment_3_out_10),
    .col21(videosegment_3_out_11), .col22(videosegment_3_out_12), .col23(videosegment_3_out_13),
    .col24(videosegment_4_out_6), .col25(videosegment_4_out_7), .col26(videosegment_4_out_8),
    .col27(videosegment_4_out_9), .col28(videosegment_4_out_10), .col29(videosegment_4_out_11),
    .col30(videosegment_4_out_12), .col31(videosegment_4_out_13));
  videosegment videosegment_1 (
    .in_1(controlchip_1_zero), .in_2(controlchip_1_ballx), .in_3(controlchip_1_bally),
    .in_4(controlchip_1_leftyout), .in_5(controlchip_1_rightyout), .out_14(videosegment_1_out_14),
    .out_15(videosegment_1_out_15), .out_16(videosegment_1_out_16), .out_17(videosegment_1_out_17),
    .out_18(videosegment_1_out_18), .out_6(videosegment_1_out_6), .out_7(videosegment_1_out_7),
    .out_8(videosegment_1_out_8), .out_9(videosegment_1_out_9), .out_10(videosegment_1_out_10),
    .out_11(videosegment_1_out_11), .out_12(videosegment_1_out_12), .out_13(videosegment_1_out_13));
  videosegment videosegment_2 (
    .in_1(videosegment_1_out_14), .in_2(videosegment_1_out_15), .in_3(videosegment_1_out_16),
    .in_4(videosegment_1_out_17), .in_5(videosegment_1_out_18), .out_14(videosegment_2_out_14),
    .out_15(videosegment_2_out_15), .out_16(videosegment_2_out_16), .out_17(videosegment_2_out_17),
    .out_18(videosegment_2_out_18), .out_6(videosegment_2_out_6), .out_7(videosegment_2_out_7),
    .out_8(videosegment_2_out_8), .out_9(videosegment_2_out_9), .out_10(videosegment_2_out_10),
    .out_11(videosegment_2_out_11), .out_12(videosegment_2_out_12), .out_13(videosegment_2_out_13));
  videosegment videosegment_3 (
    .in_1(videosegment_2_out_14), .in_2(videosegment_2_out_15), .in_3(videosegment_2_out_16),
    .in_4(videosegment_2_out_17), .in_5(videosegment_2_out_18), .out_14(videosegment_3_out_14),
    .out_15(videosegment_3_out_15), .out_16(videosegment_3_out_16), .out_17(videosegment_3_out_17),
    .out_18(videosegment_3_out_18), .out_6(videosegment_3_out_6), .out_7(videosegment_3_out_7),
    .out_8(videosegment_3_out_8), .out_9(videosegment_3_out_9), .out_10(videosegment_3_out_10),
    .out_11(videosegment_3_out_11), .out_12(videosegment_3_out_12), .out_13(videosegment_3_out_13));
  Hex_Digit_Display hex_digit_display_3 (.value(Rs[3:0]));  // open: dp
  Hex_Digit_Display hex_digit_display_4 (.value(Rs[7:4]));  // open: dp
  videosegment videosegment_4 (
    .in_1(videosegment_3_out_14), .in_2(videosegment_3_out_15), .in_3(videosegment_3_out_16),
    .in_4(videosegment_3_out_17), .in_5(videosegment_3_out_18), .out_6(videosegment_4_out_6),
    .out_7(videosegment_4_out_7), .out_8(videosegment_4_out_8), .out_9(videosegment_4_out_9),
    .out_10(videosegment_4_out_10), .out_11(videosegment_4_out_11), .out_12(videosegment_4_out_12),
    .out_13(videosegment_4_out_13));  // open: out_14, out_15, out_16, out_17, out_18
endmodule

module inrange (
  input  [4:0] Yball,
  input  [4:0] Ybat,
  output shareArow
);

  wire comparator_1_eq, comparator_2_eq, comparator_3_eq;
  wire [4:0] adder_1_out, adder_2_out;

  Adder #(.width(5)) adder_1 (.a(Ybat), .b(5'b00001), .out(adder_1_out));  // open: cin, cout
  Adder #(.width(5)) adder_2 (.a(Ybat), .b(5'b00010), .out(adder_2_out));  // open: cin, cout
  Comparator #(.width(5)) comparator_1 (.a(Yball), .b(Ybat), .eq(comparator_1_eq));  // open: gt, lt
  Comparator #(.width(5)) comparator_2 (.a(Yball), .b(adder_1_out), .eq(comparator_2_eq));  // open: gt, lt
  Comparator #(.width(5)) comparator_3 (.a(Yball), .b(adder_2_out), .eq(comparator_3_eq));  // open: gt, lt
  or or_1 (shareArow, comparator_1_eq, comparator_2_eq, comparator_3_eq);
endmodule

module scores (
  input  [7:0] \input ,
  output [7:0] scoreOut
);

  wire comparator_1_gt;
  wire [7:0] adder_1_out, adder_2_out;

  Adder adder_1 (.a(8'h6), .b(adder_2_out), .out(adder_1_out));  // open: cin, cout
  Adder adder_2 (.a(\input ), .b(8'h1), .out(adder_2_out));  // open: cin, cout
  Comparator #(.width(4), .mode("unsigned")) comparator_1 (
    .a(adder_2_out[3:0]), .b(4'b1001), .gt(comparator_1_gt));  // open: eq, lt
  Multiplexer #(.width(8), .enable("false")) multiplexer_1 (
    .in0(adder_2_out), .in1(adder_1_out), .out(scoreOut), .sel(comparator_1_gt));
endmodule

module controlChip (
  input  [4:0] leftYin,
  input  Reset,
  input  Tacts,
  output [7:0] scoreB,
  output [4:0] zero,
  output [7:0] scoreA,
  output [4:0] ballX,
  output [4:0] ballY,
  output [4:0] leftYout,
  output [4:0] rightYout
);

  wire and_1_out, and_2_out, cdmRestart, comparator_1_eq, comparator_2_eq, comparator_3_eq, comparator_5_lt,
       comparator_6_gt, comparator_10_eq, comparator_10_gt, comparator_10_lt, inrange_1_sharearow,
       inrange_2_sharearow, invBot, invUp, LScore, not_1_out, or_1_out, or_2_out, Res, RScore;
  wire [1:0] random_1_out;
  wire [2:0] rightbot_1_rightbaty, X, Y;
  wire [4:0] cdmBat, controlled_buffer_1_out, controlled_buffer_2_out, controlled_buffer_3_out, register_3_q;
  wire [7:0] and_3_out, multiplexer_1_out, multiplexer_2_out, scores_1_scoreout, scores_2_scoreout, Vx;
  wire [7:3] VxyBOT, Vy;

  scores scores_1 (.scoreOut(scores_1_scoreout), .\input (scoreB));
  Register register_1 (.D(scores_1_scoreout), .Q(scoreB), .clk(LScore), .clr(Res));  // open: en
  inrange inrange_1 (.Yball(ballY), .Ybat(rightYout), .shareArow(inrange_1_sharearow));
  Comparator #(.width(5)) comparator_1 (.a(5'b11011), .b(ballX), .eq(comparator_1_eq));  // open: gt, lt
  or or_1 (or_1_out, and_2_out, LScore);
  or or_2 (or_2_out, and_1_out, RScore);
  scores scores_2 (.scoreOut(scores_2_scoreout), .\input (scoreA));
  Register register_2 (.D(scores_2_scoreout), .Q(scoreA), .clk(RScore), .clr(Res));  // open: en
  and and_1 (and_1_out, inrange_1_sharearow, comparator_1_eq);
  Comparator #(.mode("unsigned")) comparator_2 (.a(scoreA), .b(8'h5), .eq(comparator_2_eq));  // open: gt, lt
  Comparator #(.mode("unsigned")) comparator_3 (.a(scoreB), .b(8'h5), .eq(comparator_3_eq));  // open: gt, lt
  inrange inrange_2 (.Yball(ballY), .Ybat(leftYin), .shareArow(inrange_2_sharearow));
  and and_2 (and_2_out, inrange_2_sharearow, cdmRestart);
  or or_3 (Res, comparator_3_eq, comparator_2_eq, Reset);
  Comparator #(.width(5)) comparator_4 (.a(5'b00100), .b(ballX), .eq(cdmRestart));  // open: gt, lt
  ballMovementX ballmovementx_1 (
    .vx(Vx), .coordinates({ballX, X}), .velocity(8'hfe), .Restart(Res), .tact(Tacts), .left(or_1_out),
    .right(or_2_out));
  Comparator #(.mode("unsigned")) comparator_5 (.a({ballY, Y}), .b(8'h46), .lt(comparator_5_lt));  // open: gt, eq
  and and_3 (and_3_out[0], comparator_5_lt, comparator_6_gt);
  Comparator #(.mode("unsigned")) comparator_6 (.a({ballY, Y}), .b({8{1'b0}}), .gt(comparator_6_gt));  // open: eq, lt
  Comparator #(.mode("unsigned")) comparator_7 (.a({ballY, Y}), .b(8'hb0), .gt(and_3_out[7]));  // open: eq, lt
  // Probe on ballX
  Pull_Resistor pull_resistor_1 (.node(and_3_out[6]));
  Random #(.width(2), .seed(2)) random_1 (.clk(Res), .out(random_1_out));  // open: next, clr
  Comparator #(.width(5)) comparator_8 (.a(ballX), .b({5{1'b1}}), .eq(RScore));  // open: gt, lt
  Comparator #(.width(5)) comparator_9 (.a(ballX), .b({5{1'b0}}), .eq(LScore));  // open: gt, lt
  Multiplexer #(.width(8), .enable("false")) multiplexer_1 (
    .in0({8{1'b1}}), .in1(8'h1), .out(multiplexer_1_out), .sel(random_1_out[0]));
  rightBot rightbot_1 (
    .RightBatY({rightYout, rightbot_1_rightbaty}), .res(cdmRestart),
    .Vxy({{2{VxyBOT[7]}}, VxyBOT[5:3], Vx[2:0]}), .x({ballX, X}), .y({ballY, Y}),
    .allow({and_3_out[7:6], {5{and_3_out[6]}}, and_3_out[0]}));  // open: block
  not not_1 (not_1_out, ballX[4]);
  Multiplexer #(.select(2), .width(8), .enable("false")) multiplexer_2 (
    .in0(8'h7d), .in1(8'h73), .in2(8'h69), .in3(8'h96), .out(multiplexer_2_out), .sel(random_1_out));
  ballMovementY ballmovementy_1 (
    .velocity(multiplexer_1_out), .Restart(Res), .tact(Tacts), .reflectUp(invUp), .coordinates({ballY, Y}),
    .reflectBot(invBot), .startY(multiplexer_2_out), .vy({Vy, VxyBOT[5:3]}));
  Comparator #(.width(5), .mode("unsigned")) comparator_10 (
    .a(cdmBat), .b(rightYout), .gt(comparator_10_gt), .eq(comparator_10_eq), .lt(comparator_10_lt));
  Pull_Resistor pull_resistor_2 (.node(VxyBOT[7]));
  Comparator #(.width(5)) comparator_11 (.a(ballY), .b({5{1'b0}}), .eq(invBot));  // open: gt, lt
  Comparator #(.width(5)) comparator_12 (.a(ballY), .b({5{1'b1}}), .eq(invUp));  // open: gt, lt
  assign controlled_buffer_1_out = comparator_10_gt ? rightYout : 5'bz;  // Controlled_Buffer controlled_buffer_1
  assign controlled_buffer_2_out = comparator_10_lt ? rightYout : 5'bz;  // Controlled_Buffer controlled_buffer_2
  assign controlled_buffer_3_out = comparator_10_eq ? rightYout : 5'bz;  // Controlled_Buffer controlled_buffer_3
  Adder #(.width(5)) adder_1 (
    .a(controlled_buffer_1_out), .b(5'b00001), .out(controlled_buffer_3_out));  // open: cin, cout
  Adder #(.width(5)) adder_2 (
    .a(controlled_buffer_2_out), .b({5{1'b1}}), .out(controlled_buffer_3_out));  // open: cin, cout
  Register #(.width(5)) register_3 (.D(controlled_buffer_3_out), .Q(register_3_q), .clk(Tacts));  // open: en, clr

  assign leftYout = leftYin;
  assign zero = {5{1'b0}};

  // Other names for the same wires on the sheet: rBat[4:0] = rightYout; X[7:3] = ballX; Y[7:3] = ballY;
  //   lBat[4:0] = leftYin; tact = Tacts; VxyBOT (some bits) = {VxyBOT[7], Vx[2:0]}; Vy[2:0] = VxyBOT[5:3]

  // Notes on the sheet:
  //   RIGHT ROCKET COLLISION
  //   LEFT ROCKET COLLISION
  //   RAND COORD Y
  //   CDM8
  //   ball's velocity for cdm8
  //   input
  //   output
endmodule

module velInvert (
  input  [7:0] in_1,
  output [7:0] out_2
);

  // Probe on in_1
  // Probe on out_2
  Negator negator_1 (.in(in_1), .out(out_2));
endmodule

module ballMovementX (
  input  [7:0] velocity,
  input  Restart,
  input  tact,
  input  left,
  input  right,
  output [7:0] vx,
  output [7:0] coordinates
);

  wire and_1_out, and_2_out, not_1_out, or_1_out;
  wire [7:0] adder_1_out, multiplexer_1_out, multiplexer_2_out, multiplexer_3_out, velinvert_1_out_2;

  // Probe on velinvert_1_out_2
  // Probe on vx
  velInvert velinvert_1 (.in_1(vx), .out_2(velinvert_1_out_2));
  Multiplexer #(.width(8), .enable("false")) multiplexer_1 (
    .in0(vx), .in1(velinvert_1_out_2), .out(multiplexer_1_out), .sel(or_1_out));
  or or_1 (or_1_out, and_2_out, and_1_out);
  Register register_1 (.D(multiplexer_2_out), .Q(vx), .clk(tact));  // open: en, clr
  Multiplexer #(.width(8), .enable("false")) multiplexer_2 (
    .in0(multiplexer_1_out), .in1(velocity), .out(multiplexer_2_out), .sel(Restart));
  not not_1 (not_1_out, vx[7]);
  and and_1 (and_1_out, not_1_out, right);
  and and_2 (and_2_out, left, vx[7]);
  Adder adder_1 (.a(coordinates), .b(vx), .out(adder_1_out));  // open: cin, cout
  Multiplexer #(.width(8), .enable("false")) multiplexer_3 (
    .in0(adder_1_out), .in1(8'h80), .out(multiplexer_3_out), .sel(Restart));
  Register register_2 (.D(multiplexer_3_out), .Q(coordinates), .clk(tact));  // open: en, clr

  // Other names for the same wires on the sheet: vel[7:0] = velocity

  // Notes on the sheet:
  //   2 /  -2
  //   start
endmodule

module ballMovementY (
  input  [7:0] startY,
  input  [7:0] velocity,
  input  Restart,
  input  tact,
  input  reflectUp,
  input  reflectBot,
  output [7:0] vy,
  output [7:0] coordinates
);

  wire and_1_out, and_2_out, not_1_out, or_1_out;
  wire [7:0] adder_1_out, multiplexer_1_out, multiplexer_2_out, multiplexer_3_out, velinvert_1_out_2;

  velInvert velinvert_1 (.in_1(vy), .out_2(velinvert_1_out_2));
  Multiplexer #(.width(8), .enable("false")) multiplexer_1 (
    .in0(vy), .in1(velinvert_1_out_2), .out(multiplexer_1_out), .sel(or_1_out));
  Multiplexer #(.width(8), .enable("false")) multiplexer_2 (
    .in0(multiplexer_1_out), .in1(velocity), .out(multiplexer_2_out), .sel(Restart));
  or or_1 (or_1_out, and_1_out, and_2_out);
  Register register_1 (.D(multiplexer_2_out), .Q(vy), .clk(tact));  // open: en, clr
  and and_1 (and_1_out, vy[7], reflectBot);
  and and_2 (and_2_out, reflectUp, not_1_out);
  not not_1 (not_1_out, vy[7]);
  Adder adder_1 (.a(coordinates), .b(vy), .out(adder_1_out));  // open: cin, cout
  Multiplexer #(.width(8), .enable("false")) multiplexer_3 (
    .in0(adder_1_out), .in1(startY), .out(multiplexer_3_out), .sel(Restart));
  Register register_2 (.D(multiplexer_3_out), .Q(coordinates), .clk(tact));  // open: en, clr

  // Other names for the same wires on the sheet: inverseBot = reflectBot; inverseUp = reflectUp; vel[7:0] = velocity

  // Notes on the sheet:
  //   1 / -1
  //   start
endmodule

module rightBot (
  input  res,
  input  block,
  input  [7:0] Vxy,
  input  [7:0] x,
  input  [7:0] y,
  input  [7:0] allow,
  output [7:0] RightBatY
);

  wire _0xF1_out, _0xF2_out, _0xF3_out, _0xF4_out, _0xFF_out, cdm_8_mark5_1_data_inst, Cl, code, data,
       decoder_2_out1, decoder_2_out2, decoder_2_out3, decoder_2_out4, decoder_2_out15, I_Osel, In_out_prime,
       mem, nand_1_out, nor_1_out, not_1_out, not_2_out, RAM;
  wire [3:0] I_Oadr;
  wire [7:0] cdm_8_mark5_1_data_out, cdm_8_mark5_1_pc, cdm_8_mark5_1_ps, cdm_8_mark5_1_r0, cdm_8_mark5_1_r1,
       cdm_8_mark5_1_r2, cdm_8_mark5_1_r3, cdm_8_mark5_1_sp, controlled_buffer_1_out, I_Odat;
  wire [7:4] cdm_8_mark5_1_addr;

  and and_1 (I_Osel, not_1_out, Cl, data);
  // Probe on cdm_8_mark5_1_r3
  // Probe on cdm_8_mark5_1_r2
  // Probe on cdm_8_mark5_1_r1
  // Probe on cdm_8_mark5_1_pc
  // Probe on cdm_8_mark5_1_r0
  Clock clock_1 (.out(Cl));
  not not_1 (not_1_out, nand_1_out);
  nand nand_1 (nand_1_out, cdm_8_mark5_1_addr[4], cdm_8_mark5_1_addr[5], cdm_8_mark5_1_addr[6], cdm_8_mark5_1_addr[7]);
  and and_2 (RAM, nand_1_out, data);
  // Probe on cdm_8_mark5_1_ps
  // Probe on cdm_8_mark5_1_sp
  CdM_8_mark5 cdm_8_mark5_1 (
    .clock(Cl), .addr({cdm_8_mark5_1_addr, I_Oadr}), .mem_read(In_out_prime), .mem_cycle(mem),
    .data_inst(cdm_8_mark5_1_data_inst), .data_out(cdm_8_mark5_1_data_out),
    .data_in(controlled_buffer_1_out), .r0(cdm_8_mark5_1_r0), .r1(cdm_8_mark5_1_r1), .r2(cdm_8_mark5_1_r2),
    .r3(cdm_8_mark5_1_r3), .PC(cdm_8_mark5_1_pc), .SP(cdm_8_mark5_1_sp), .PS(cdm_8_mark5_1_ps), .reset(res));  // open: IAck, IRQ, vec
  assign controlled_buffer_1_out = In_out_prime ? I_Odat : 8'bz;  // Controlled_Buffer controlled_buffer_1
  Decoder decoder_1 (.out0(code), .out1(data), .sel(cdm_8_mark5_1_data_inst), .en(mem));
  assign I_Odat = not_2_out ? cdm_8_mark5_1_data_out : 8'bz;  // Controlled_Buffer controlled_buffer_2
  not not_2 (not_2_out, In_out_prime);
  Pull_Resistor pull_resistor_1 (.node(I_Oadr[0]));
  Pull_Resistor pull_resistor_2 (.node(I_Oadr[1]));
  Pull_Resistor pull_resistor_3 (.node(I_Oadr[2]));
  Pull_Resistor pull_resistor_4 (.node(I_Oadr[3]));
  Pull_Resistor pull_resistor_5 (.node(cdm_8_mark5_1_addr[4]));
  Pull_Resistor pull_resistor_6 (.node(cdm_8_mark5_1_addr[5]));
  Pull_Resistor pull_resistor_7 (.node(cdm_8_mark5_1_addr[6]));
  Pull_Resistor pull_resistor_8 (.node(cdm_8_mark5_1_addr[7]));
  ROM rom_1 (.addr({cdm_8_mark5_1_addr, I_Oadr}), .data(I_Odat), .sel(code));
  RAM #(.bus("separate")) ram_1 (
    .addr({cdm_8_mark5_1_addr, I_Oadr}), .din(I_Odat), .data(I_Odat), .sel(RAM), .clk(Cl), .ld(In_out_prime),
    .clr(res));  // open: str
  Decoder #(.select(4), .enable("false")) decoder_2 (
    .out1(decoder_2_out1), .out2(decoder_2_out2), .out3(decoder_2_out3), .out4(decoder_2_out4),
    .out15(decoder_2_out15), .sel(I_Oadr));  // open: out0, out5, out6, out7, out8, out9, out10, out11, out12, out13, out14
  and _0xF1 (_0xF1_out, decoder_2_out1, ~In_out_prime, I_Osel);  // AND_Gate
  and _0xF4 (_0xF4_out, decoder_2_out4, In_out_prime, I_Osel);
  and _0xF3 (_0xF3_out, decoder_2_out3, In_out_prime, I_Osel);
  and _0xF2 (_0xF2_out, decoder_2_out2, In_out_prime, I_Osel);
  and _0xFF (_0xFF_out, decoder_2_out15, In_out_prime, I_Osel);
  assign I_Odat = _0xF4_out ? Vxy : 8'bz;  // Controlled_Buffer controlled_buffer_3
  assign I_Odat = _0xF3_out ? x : 8'bz;  // Controlled_Buffer controlled_buffer_4
  assign I_Odat = _0xF2_out ? y : 8'bz;  // Controlled_Buffer controlled_buffer_5
  assign I_Odat = _0xFF_out ? allow : 8'bz;  // Controlled_Buffer controlled_buffer_6
  nor nor_1 (nor_1_out, _0xF1_out, _0xF4_out, _0xFF_out, _0xF3_out, _0xF2_out);
  and and_3 (RAM, nor_1_out, data);
  Register register_1 (.D(I_Odat), .en(block), .Q(RightBatY), .clk(_0xF1_out));  // open: clr

  // Other names for the same wires on the sheet: rd_wr_prime = In_out_prime

  // Notes on the sheet:
  //   contents of rom_1 (hex, n*v repeats v):
  //   cd f0 d0 f2 d1 f3 d2 f4 d3 ff b0 b5 ba bf c3 d3 e0 3d 5 91 d3 20 4b f e0 1f 85 d3 0 ee 21 d3 1 c6 c1
  //   9 a e5 37 f e0 35 c5 11 85 89 89 89 d3 f1 ad ee 2 ee 49 d2 1 46 e0 49 f e1 49 c5 8d 8d 11 85 d3 f1
  //   ad ee 2 c5 11 d3 f1 ad ee 2 d4
endmodule
